// Logisim project Adding-Subtracting.circ as structural Verilog: 1 circuit, main circuit main
module main (
  input  in_1,
  input  in_2,
  input  in_3,
  input  Sign_A,
  input  Sign_B,
  input  B1,
  input  in_7,
  input  B0,
  input  in_9,
  input  Opr0,
  output Out_3,
  output Out_2,
  output Out_1,
  output out_14,
  output Out_sign
);

  wire adder_1_cout, adder_1_out, adder_2_cout, adder_2_out, adder_3_cout, adder_3_out, adder_4_cout,
       adder_5_cout, and_1_out, and_2_out, and_3_out, and_4_out, and_6_out, not_1_out, not_2_out, not_3_out,
       xor_1_out, xor_2_out, xor_3_out, xor_4_out, xor_5_out, xor_6_out, xor_7_out, xor_8_out, xor_9_out,
       xor_10_out, xor_11_out;

  and and_1 (and_1_out, not_1_out, Opr0);
  not not_1 (not_1_out, in_9);
  xor xor_1 (xor_1_out, Sign_B, and_1_out);
  and and_2 (and_2_out, Sign_A, xor_1_out);
  xor xor_2 (xor_2_out, Sign_A, xor_1_out);
  and and_3 (and_3_out, Sign_A, xor_2_out);
  and and_4 (and_4_out, xor_2_out, xor_1_out);
  xor xor_3 (xor_3_out, and_3_out, in_1);
  xor xor_4 (xor_4_out, and_4_out, B1);
  xor xor_5 (xor_5_out, and_3_out, in_2);
  xor xor_6 (xor_6_out, and_3_out, in_3);
  xor xor_7 (xor_7_out, and_4_out, in_7);
  not not_2 (not_2_out, xor_2_out);
  xor xor_8 (xor_8_out, and_4_out, B0);
  Adder #(.width(1)) adder_1 (.a(xor_8_out), .b(xor_6_out), .out(adder_1_out), .cin(xor_2_out), .cout(adder_1_cout));
  Adder #(.width(1)) adder_2 (.a(xor_5_out), .b(xor_7_out), .out(adder_2_out), .cin(adder_1_cout), .cout(adder_2_cout));
  Adder #(.width(1)) adder_3 (.a(xor_4_out), .b(xor_3_out), .out(adder_3_out), .cin(adder_2_cout), .cout(adder_3_cout));
  not not_3 (not_3_out, adder_3_cout);
  and and_5 (Out_3, adder_3_cout, not_2_out);
  and and_6 (and_6_out, xor_2_out, not_3_out);
  xor xor_9 (xor_9_out, adder_1_out, and_6_out);
  xor xor_10 (xor_10_out, adder_2_out, and_6_out);
  xor xor_11 (xor_11_out, adder_3_out, and_6_out);
  xor xor_12 (Out_sign, and_6_out, and_2_out);
  Adder #(.width(1)) adder_4 (.a(1'b0), .b(xor_9_out), .out(out_14), .cin(and_6_out), .cout(adder_4_cout));
  Adder #(.width(1)) adder_5 (.a(1'b0), .b(xor_10_out), .out(Out_1), .cin(adder_4_cout), .cout(adder_5_cout));
  Adder #(.width(1)) adder_6 (.a(1'b0), .b(xor_11_out), .out(Out_2), .cin(adder_5_cout));  // open: cout

  // Notes on the sheet:
  //   Opr1
  //   B2
  //   A2
  //   A1
  //   A0
  //   Out 0
endmodule
