// Logisim project Counter CMOS.circ as structural Verilog: 5 circuits, main circuit main
module main (
  input  UP_DOWN,
  input  CLOCK,
  output Out1,
  output out_4,
  output Out0
);

  wire and_1_out, and_2_out, and_3_out, and_4_out, j_k_ff_1_qn, j_k_ff_2_qn, not_1_out, or_1_out, or_2_out;

  J_K_Flip_Flop_part #(.trigger("falling")) j_k_ff_1 (
    .J(1'b1), .clk(CLOCK), .K(1'b1), .Q(Out0), .Qn(j_k_ff_1_qn));  // open: preset, en, reset
  not not_1 (not_1_out, UP_DOWN);
  and and_1 (and_1_out, UP_DOWN, Out0);
  and and_2 (and_2_out, j_k_ff_1_qn, not_1_out);
  or or_1 (or_1_out, and_1_out, and_2_out);
  J_K_Flip_Flop_part #(.trigger("falling")) j_k_ff_2 (
    .J(or_1_out), .clk(CLOCK), .K(or_1_out), .Q(out_4), .Qn(j_k_ff_2_qn));  // open: preset, en, reset
  and and_3 (and_3_out, and_1_out, out_4);
  and and_4 (and_4_out, j_k_ff_2_qn, and_2_out);
  or or_2 (or_2_out, and_3_out, and_4_out);
  J_K_Flip_Flop_part #(.trigger("falling")) j_k_ff_3 (
    .J(or_2_out), .clk(CLOCK), .K(or_2_out), .Q(Out1));  // open: Qn, preset, en, reset

  // Notes on the sheet:
  //   1:UP
  //   0:Down
  //   Out2
endmodule

module AND (
  input  in_1,
  input  in_2,
  output out_3
);

  Transistor #(.\type ("n")) transistor_1 (.in(in_2), .out(out_3), .gate(in_1));
  Transistor #(.gate("br")) transistor_2 (.in(1'b0), .out(out_3), .gate(in_1));
endmodule

module NOT (
  input  in_1,
  output out_2
);

  Transistor transistor_1 (.in(1'b1), .out(out_2), .gate(in_1));
  Transistor #(.\type ("n"), .gate("br")) transistor_2 (.in(1'b0), .out(out_2), .gate(in_1));
endmodule

module R_S_Latch (
  input  Reset,
  input  Set,
  output Q,
  output Q_prime
);

  wire and_1_out_3, and_2_out_3;

  AND and_1 (.in_2(Q_prime), .in_1(Reset), .out_3(and_1_out_3));
  AND and_2 (.in_2(Q), .in_1(Set), .out_3(and_2_out_3));
  NOT not_1 (.in_1(and_1_out_3), .out_2(Q));
  NOT not_2 (.in_1(and_2_out_3), .out_2(Q_prime));
endmodule

module J_K_Flip_Flop (
  input  in_1,
  input  CLK,
  input  in_3
);

  wire and_1_out_3, and_2_out_3, and_3_out_3, and_4_out_3, and_5_out_3, and_6_out_3, not_1_out_2,
       not_2_out_2, not_3_out_2, not_4_out_2, r_s_latch_1_q, r_s_latch_1_q_prime, r_s_latch_2_q,
       r_s_latch_2_q_prime;

  AND and_1 (.in_2(r_s_latch_2_q_prime), .in_1(in_3), .out_3(and_1_out_3));
  NOT not_1 (.in_1(and_4_out_3), .out_2(not_1_out_2));
  AND and_2 (.in_2(and_1_out_3), .in_1(CLK), .out_3(and_2_out_3));
  AND and_3 (.in_2(r_s_latch_2_q), .in_1(in_1), .out_3(and_3_out_3));
  AND and_4 (.in_2(CLK), .in_1(and_3_out_3), .out_3(and_4_out_3));
  R_S_Latch r_s_latch_1 (.Reset(not_1_out_2), .Set(not_2_out_2), .Q(r_s_latch_1_q), .Q_prime(r_s_latch_1_q_prime));
  NOT not_2 (.in_1(and_2_out_3), .out_2(not_2_out_2));
  NOT not_3 (.in_1(and_5_out_3), .out_2(not_3_out_2));
  AND and_5 (.in_2(r_s_latch_1_q), .in_1(CLK), .out_3(and_5_out_3));
  NOT not_4 (.in_1(and_6_out_3), .out_2(not_4_out_2));
  AND and_6 (.in_2(r_s_latch_1_q_prime), .in_1(CLK), .out_3(and_6_out_3));
  R_S_Latch r_s_latch_2 (.Reset(not_3_out_2), .Set(not_4_out_2), .Q(r_s_latch_2_q), .Q_prime(r_s_latch_2_q_prime));
endmodule
