// Logisim project Counter Gates.circ as structural Verilog: 1 circuit, main circuit main
module main (
  input  UP_DOWN,
  input  CLOCK,
  output Out1,
  output out_4,
  output Out0
);

  wire and_1_out, and_2_out, and_3_out, and_4_out, j_k_ff_1_qn, j_k_ff_2_qn, not_1_out, or_1_out, or_2_out;

  J_K_Flip_Flop #(.trigger("falling")) j_k_ff_1 (
    .J(1'b1), .clk(CLOCK), .K(1'b1), .Q(Out0), .Qn(j_k_ff_1_qn));  // open: preset, en, reset
  not not_1 (not_1_out, UP_DOWN);
  and and_1 (and_1_out, UP_DOWN, Out0);
  and and_2 (and_2_out, j_k_ff_1_qn, not_1_out);
  or or_1 (or_1_out, and_1_out, and_2_out);
  J_K_Flip_Flop #(.trigger("falling")) j_k_ff_2 (
    .J(or_1_out), .clk(CLOCK), .K(or_1_out), .Q(out_4), .Qn(j_k_ff_2_qn));  // open: preset, en, reset
  and and_3 (and_3_out, and_1_out, out_4);
  and and_4 (and_4_out, j_k_ff_2_qn, and_2_out);
  or or_2 (or_2_out, and_3_out, and_4_out);
  J_K_Flip_Flop #(.trigger("falling")) j_k_ff_3 (
    .J(or_2_out), .clk(CLOCK), .K(or_2_out), .Q(Out1));  // open: Qn, preset, en, reset

  // Notes on the sheet:
  //   1:UP
  //   0:Down
  //   Out2
endmodule
