// Logisim project J-K flip flop.circ as structural Verilog: 5 circuits, main circuit main
module main (
  input  in_1,
  input  in_2
);

  wire and_1_out_3, and_2_out_3, and_3_out_3, and_4_out_3, and_5_out_3, and_6_out_3, not_1_out_2,
       not_2_out_2, not_3_out_2, not_4_out_2, r_s_latch_1_q, r_s_latch_1_q_prime, r_s_latch_2_q,
       r_s_latch_2_q_prime, undriven;

  AND and_1 (.in_2(r_s_latch_2_q_prime), .in_1(in_2), .out_3(and_1_out_3));
  NOT not_1 (.in_1(and_4_out_3), .out_2(not_1_out_2));
  AND and_2 (.in_2(and_1_out_3), .in_1(undriven), .out_3(and_2_out_3));
  AND and_3 (.in_2(r_s_latch_2_q), .in_1(in_1), .out_3(and_3_out_3));
  AND and_4 (.in_2(undriven), .in_1(and_3_out_3), .out_3(and_4_out_3));
  R_S_Latch r_s_latch_1 (.Reset(not_1_out_2), .Set(not_2_out_2), .Q(r_s_latch_1_q), .Q_prime(r_s_latch_1_q_prime));
  NOT not_2 (.in_1(and_2_out_3), .out_2(not_2_out_2));
  NOT not_3 (.in_1(and_5_out_3), .out_2(not_3_out_2));
  AND and_5 (.in_2(r_s_latch_1_q), .in_1(undriven), .out_3(and_5_out_3));
  NOT not_4 (.in_1(and_6_out_3), .out_2(not_4_out_2));
  AND and_6 (.in_2(r_s_latch_1_q_prime), .in_1(undriven), .out_3(and_6_out_3));
  R_S_Latch r_s_latch_2 (.Reset(not_3_out_2), .Set(not_4_out_2), .Q(r_s_latch_2_q), .Q_prime(r_s_latch_2_q_prime));
endmodule

module AND (
  input  in_1,
  input  in_2,
  output out_3
);

  Transistor #(.\type ("n")) transistor_1 (.in(in_2), .out(out_3), .gate(in_1));
  Transistor #(.gate("br")) transistor_2 (.in(1'b0), .out(out_3), .gate(in_1));
endmodule

module NOT (
  input  in_1,
  output out_2
);

  Transistor transistor_1 (.in(1'b1), .out(out_2), .gate(in_1));
  Transistor #(.\type ("n"), .gate("br")) transistor_2 (.in(1'b0), .out(out_2), .gate(in_1));
endmodule

module R_S_Latch (
  input  Reset,
  input  Set,
  output Q,
  output Q_prime
);

  wire and_1_out_3, and_2_out_3;

  AND and_1 (.in_2(Q_prime), .in_1(Reset), .out_3(and_1_out_3));
  AND and_2 (.in_2(Q), .in_1(Set), .out_3(and_2_out_3));
  NOT not_1 (.in_1(and_1_out_3), .out_2(Q));
  NOT not_2 (.in_1(and_2_out_3), .out_2(Q_prime));
endmodule

module J_K_Flip_Flop (
  input  in_1,
  input  CLK,
  input  in_3
);

  wire and_1_out_3, and_2_out_3, and_3_out_3, and_4_out_3, and_5_out_3, and_6_out_3, not_1_out_2,
       not_2_out_2, not_3_out_2, not_4_out_2, r_s_latch_1_q, r_s_latch_1_q_prime, r_s_latch_2_q,
       r_s_latch_2_q_prime;

  AND and_1 (.in_2(r_s_latch_2_q_prime), .in_1(in_3), .out_3(and_1_out_3));
  NOT not_1 (.in_1(and_4_out_3), .out_2(not_1_out_2));
  AND and_2 (.in_2(and_1_out_3), .in_1(CLK), .out_3(and_2_out_3));
  AND and_3 (.in_2(r_s_latch_2_q), .in_1(in_1), .out_3(and_3_out_3));
  AND and_4 (.in_2(CLK), .in_1(and_3_out_3), .out_3(and_4_out_3));
  R_S_Latch r_s_latch_1 (.Reset(not_1_out_2), .Set(not_2_out_2), .Q(r_s_latch_1_q), .Q_prime(r_s_latch_1_q_prime));
  NOT not_2 (.in_1(and_2_out_3), .out_2(not_2_out_2));
  NOT not_3 (.in_1(and_5_out_3), .out_2(not_3_out_2));
  AND and_5 (.in_2(r_s_latch_1_q), .in_1(CLK), .out_3(and_5_out_3));
  NOT not_4 (.in_1(and_6_out_3), .out_2(not_4_out_2));
  AND and_6 (.in_2(r_s_latch_1_q_prime), .in_1(CLK), .out_3(and_6_out_3));
  R_S_Latch r_s_latch_2 (.Reset(not_3_out_2), .Set(not_4_out_2), .Q(r_s_latch_2_q), .Q_prime(r_s_latch_2_q_prime));
endmodule
