// Logisim project Up-down_Counter_Design-in-Gates.circ as structural Verilog: 1 circuit, main circuit main
module main (
  input  UP_DOWN,
  input  CLOCK,
  output Out1,
  output out_4,
  output out_5
);

  wire j_k_ff_1_qn, j_k_ff_2_qn, nand_1_out, nand_2_out, nand_3_out, nand_4_out, nand_5_out, nand_6_out,
       not_1_out, not_2_out, not_3_out;

  J_K_Flip_Flop #(.trigger("falling")) j_k_ff_1 (
    .J(1'b1), .clk(CLOCK), .K(1'b1), .Q(out_5), .Qn(j_k_ff_1_qn));  // open: preset, en, reset
  not not_1 (not_1_out, UP_DOWN);
  nand nand_1 (nand_1_out, UP_DOWN, out_5);
  nand nand_2 (nand_2_out, j_k_ff_1_qn, not_1_out);
  not not_2 (not_2_out, nand_1_out);
  nand nand_3 (nand_3_out, nand_1_out, nand_2_out);
  not not_3 (not_3_out, nand_2_out);
  J_K_Flip_Flop #(.trigger("falling")) j_k_ff_2 (
    .J(nand_3_out), .clk(CLOCK), .K(nand_3_out), .Q(out_4), .Qn(j_k_ff_2_qn));  // open: preset, en, reset
  nand nand_4 (nand_4_out, not_2_out, out_4);
  nand nand_5 (nand_5_out, j_k_ff_2_qn, not_3_out);
  nand nand_6 (nand_6_out, nand_4_out, nand_5_out);
  J_K_Flip_Flop #(.trigger("falling")) j_k_ff_3 (
    .J(nand_6_out), .clk(CLOCK), .K(nand_6_out), .Q(Out1));  // open: Qn, preset, en, reset

  // Notes on the sheet:
  //   1:UP
  //   0:Down
  //   Out2
  //   Out0
endmodule
