// Logisim project multiplier_CMOS.circ as structural Verilog: 7 circuits, main circuit main
module main (
  input  [2:0] A,
  input  [2:0] B,
  output [5:0] result
);

  wire [1:0] cmosand_8_outand;
  wire [2:0] cmosand_2_outand, cmosand_6_outand, n3_bit_adder_cmos_2_out_3bitadder;

  CmosAnd cmosand_1 (.outAnd(cmosand_2_outand[2]), .input1(B[2]), .input2(A[2]));
  CmosAnd cmosand_2 (.outAnd(cmosand_2_outand[0]), .input1(B[2]), .input2(A[0]));
  CmosAnd cmosand_3 (.outAnd(cmosand_2_outand[1]), .input1(B[2]), .input2(A[1]));
  _3_bit_adder_CMOS u_3_bit_adder_cmos_1 (
    .in1(n3_bit_adder_cmos_2_out_3bitadder), .in2(cmosand_2_outand), .out_3bitAdder(result[4:2]),
    .Cout(result[5]));
  CmosAnd cmosand_4 (.outAnd(cmosand_6_outand[2]), .input1(B[1]), .input2(A[2]));
  CmosAnd cmosand_5 (.outAnd(cmosand_6_outand[1]), .input1(B[1]), .input2(A[1]));
  _3_bit_adder_CMOS u_3_bit_adder_cmos_2 (
    .in1({1'b0, cmosand_8_outand}), .in2(cmosand_6_outand),
    .out_3bitAdder({n3_bit_adder_cmos_2_out_3bitadder[1:0], result[1]}),
    .Cout(n3_bit_adder_cmos_2_out_3bitadder[2]));
  CmosAnd cmosand_6 (.outAnd(cmosand_6_outand[0]), .input1(B[1]), .input2(A[0]));
  CmosAnd cmosand_7 (.outAnd(cmosand_8_outand[1]), .input1(B[0]), .input2(A[2]));
  CmosAnd cmosand_8 (.outAnd(cmosand_8_outand[0]), .input1(B[0]), .input2(A[1]));
  CmosAnd cmosand_9 (.outAnd(result[0]), .input1(B[0]), .input2(A[0]));

  // Other names for the same wires on the sheet: out1 = result[1]; out0 = result[0]; out234[2:0] = result[4:2];
  //   out5 = result[5]
endmodule

module CmosAnd (
  input  input1,
  input  input2,
  output outAnd
);

  wire transistor_1_out, transistor_3_out;

  Transistor transistor_1 (.in(1'b1), .out(transistor_1_out), .gate(input1));
  Transistor #(.\type ("n")) transistor_2 (.in(transistor_3_out), .out(transistor_1_out), .gate(input1));
  Transistor #(.\type ("n")) transistor_3 (.in(1'b0), .out(transistor_3_out), .gate(input2));
  Transistor transistor_4 (.in(1'b1), .out(transistor_1_out), .gate(input2));
  Transistor transistor_5 (.in(1'b1), .out(outAnd), .gate(transistor_1_out));
  Transistor #(.\type ("n")) transistor_6 (.in(1'b0), .out(outAnd), .gate(transistor_1_out));

  // Other names for the same wires on the sheet: A = input1; B = input2
endmodule

module CmosNot (
  input  \input ,
  output outNot
);

  Transistor transistor_1 (.in(1'b1), .out(outNot), .gate(\input ));
  Transistor #(.\type ("n")) transistor_2 (.in(1'b0), .out(outNot), .gate(\input ));
endmodule

module CMOSXor (
  input  input1,
  input  input2,
  output outXOR
);

  wire A_t, B_t, transistor_1_out, transistor_4_out, transistor_8_out;

  CmosNot cmosnot_1 (.\input (input1), .outNot(A_t));
  CmosNot cmosnot_2 (.\input (input2), .outNot(B_t));
  Transistor transistor_1 (.in(1'b1), .out(transistor_1_out), .gate(input1));
  Transistor transistor_2 (.in(transistor_1_out), .out(outXOR), .gate(A_t));
  Transistor #(.\type ("n")) transistor_3 (.in(transistor_4_out), .out(outXOR), .gate(A_t));
  Transistor #(.\type ("n")) transistor_4 (.in(1'b0), .out(transistor_4_out), .gate(B_t));
  Transistor transistor_5 (.in(1'b1), .out(transistor_1_out), .gate(input2));
  Transistor transistor_6 (.in(transistor_1_out), .out(outXOR), .gate(B_t));
  Transistor #(.\type ("n")) transistor_7 (.in(transistor_8_out), .out(outXOR), .gate(input1));
  Transistor #(.\type ("n")) transistor_8 (.in(1'b0), .out(transistor_8_out), .gate(input2));

  // Other names for the same wires on the sheet: A = input1; B = input2
endmodule

module HA_CMOS (
  input  in1,
  input  in2,
  output outHA,
  output carry
);

  CMOSXor cmosxor_1 (.input1(in1), .input2(in2), .outXOR(outHA));
  CmosAnd cmosand_1 (.outAnd(carry), .input1(in2), .input2(in1));
endmodule

module FA_CMOS (
  input  in1,
  input  in2,
  input  Cin,
  output outFA,
  output Cout
);

  wire A, B, ha_cmos_1_outha, transistor_1_out, transistor_2_out;

  HA_CMOS ha_cmos_1 (.in1(in1), .in2(in2), .outHA(ha_cmos_1_outha), .carry(A));
  HA_CMOS ha_cmos_2 (.in1(ha_cmos_1_outha), .in2(Cin), .outHA(outFA), .carry(B));
  Transistor transistor_1 (.in(1'b1), .out(transistor_1_out), .gate(A));
  Transistor transistor_2 (.in(transistor_1_out), .out(transistor_2_out), .gate(B));
  Transistor #(.\type ("n")) transistor_3 (.in(1'b0), .out(transistor_2_out), .gate(A));
  Transistor #(.\type ("n")) transistor_4 (.in(1'b0), .out(transistor_2_out), .gate(B));
  Transistor transistor_5 (.in(1'b1), .out(Cout), .gate(transistor_2_out));
  Transistor #(.\type ("n")) transistor_6 (.in(1'b0), .out(Cout), .gate(transistor_2_out));
endmodule

module _3_bit_adder_CMOS (
  input  [2:0] in1,
  input  [2:0] in2,
  output [2:0] out_3bitAdder,
  output Cout
);

  wire fa_cmos_1_cout, fa_cmos_2_cout;

  FA_CMOS fa_cmos_1 (.in1(in1[0]), .in2(in2[0]), .Cout(fa_cmos_1_cout), .outFA(out_3bitAdder[0]), .Cin(1'b0));
  FA_CMOS fa_cmos_2 (.in1(in1[1]), .in2(in2[1]), .Cout(fa_cmos_2_cout), .outFA(out_3bitAdder[1]), .Cin(fa_cmos_1_cout));
  FA_CMOS fa_cmos_3 (.in1(in1[2]), .in2(in2[2]), .Cout(Cout), .outFA(out_3bitAdder[2]), .Cin(fa_cmos_2_cout));

  // Other names for the same wires on the sheet: A0 = in1[0]; A1 = in1[1]; A2 = in1[2]; B0 = in2[0]; B1 = in2[1];
  //   B2 = in2[2]
endmodule
