// Logisim project multiplier_gates.circ as structural Verilog: 2 circuits, main circuit main
module main (
  input  [2:0] A,
  input  [2:0] B,
  output [5:0] result
);

  wire [1:0] and_9_out;
  wire [2:0] and_2_out, and_6_out, n3_bit_adder_2_output;

  and and_1 (and_2_out[2], B[2], A[2]);
  and and_2 (and_2_out[0], B[2], A[0]);
  and and_3 (and_2_out[1], B[2], A[1]);
  _3_bit_adder u_3_bit_adder_1 (
    .Cin(1'b0), .A(n3_bit_adder_2_output), .B(and_2_out), .Cout(result[5]), .\output (result[4:2]));
  and and_4 (and_6_out[2], B[1], A[2]);
  and and_5 (and_6_out[1], B[1], A[1]);
  _3_bit_adder u_3_bit_adder_2 (
    .Cin(1'b0), .A({1'b0, and_9_out}), .B(and_6_out), .Cout(n3_bit_adder_2_output[2]),
    .\output ({n3_bit_adder_2_output[1:0], result[1]}));
  and and_6 (and_6_out[0], B[1], A[0]);
  and and_7 (and_9_out[1], B[0], A[2]);
  and and_8 (result[0], B[0], A[0]);
  and and_9 (and_9_out[0], B[0], A[1]);

  // Other names for the same wires on the sheet: out1 = result[1]; out0 = result[0]; out234[2:0] = result[4:2];
  //   out5 = result[5]
endmodule

module _3_bit_adder (
  input  Cin,
  input  [2:0] A,
  input  [2:0] B,
  output [2:0] \output ,
  output Cout
);

  Adder #(.width(3)) adder_1 (.a(A), .b(B), .out(\output ), .cin(Cin), .cout(Cout));
endmodule
